# Fritzing sketch 4digitPW_AccessSys (saved by Fritzing 0.9.10b)
breadboards: 1

parts:
  Part1 = Arduino Uno (Rev3)
  16x2_LCD = LCD screen
  R1 = Rotary Potentiometer (Large) [maximum_resistance=10kΩ knob_status=50% power=0.5W package=THT]
  "1" = Pushbutton [package="[THT]"]
  "2" = Pushbutton [package="[THT]"]
  "3" = Pushbutton [package="[THT]"]
  "4" = Pushbutton [package="[THT]"]
  RED_LED = LED - 5mm [color="Red (633nm)" current=30mA package="5 mm [THT]"]
  Passive_Buzzer = Piezo Speaker
  GREEN_LED = LED - 5mm [color="Green (565nm)" current=30mA package="5 mm [THT]"]
  R2 = Resistor [tolerance=±5% power=0.25 resistance=220 package=THT]
  R3 = Resistor [tolerance=±5% power=0.25 resistance=220 package=THT]
  R4 = Resistor [tolerance=±5% power=0.25 resistance=220 package=THT]
  R5 = Resistor [tolerance=±5% power=0.25 resistance=1k package=THT]
  R6 = Resistor [tolerance=±5% power=0.25 resistance=1k package=THT]
  R7 = Resistor [tolerance=±5% power=0.25 resistance=1k package=THT]
  R8 = Resistor [tolerance=±5% power=0.25 resistance=1k package=THT]

nets:
  N1: Part1.A0, R3.Pin_1
  N2: Part1.A1, "1".Pin_3, "1".Pin_4, R5.Pin_1
  N3: Part1.A2, "2".Pin_3, "2".Pin_4, R6.Pin_1
  N4: Part1.A3, "3".Pin_3, "3".Pin_4, R7.Pin_1
  N5: Part1.A4/SDA, "4".Pin_3, "4".Pin_4, R8.Pin_1
  N6: Part1.A5/SCL, R2.Pin_1
  N7: Part1.D12/MISO, 16x2_LCD.E
  N8: Part1.D13/SCK, 16x2_LCD.RS
  N9: Part1.D2, 16x2_LCD.DB7
  N10: Part1.D3_PWM, 16x2_LCD.DB6
  N11: Part1.D4, 16x2_LCD.DB5
  N12: Part1.D5_PWM, 16x2_LCD.DB4
  N13: Part1.D6_PWM, R4.Pin_1
  5V: Part1.5V, 16x2_LCD.VDD, 16x2_LCD.LED+, R1.wiper, "1".Pin_1, "1".Pin_2, "2".Pin_1, "2".Pin_2, "3".Pin_1, "3".Pin_2, "4".Pin_1, "4".Pin_2
  GND: Part1.GND, 16x2_LCD.VSS, 16x2_LCD.R/W, 16x2_LCD.LED-, R1.leg1, RED_LED.cathode, Passive_Buzzer.pin1, GREEN_LED.cathode, R5.Pin_0, R6.Pin_0, R7.Pin_0, R8.Pin_0
  N14: 16x2_LCD.V0, R1.leg2
  N15: RED_LED.anode, R3.Pin_0
  N16: Passive_Buzzer.pin2, R2.Pin_0
  N17: GREEN_LED.anode, R4.Pin_0
